# Fritzing sketch Power board (saved by Fritzing 0.9.3b)
circuit board: 5.09722cm x 3.43736cm
breadboards: 1

parts:
  LM2 = RioRand LM2596
  J3 = Screw terminal - 2 pins [package=THT]
  JP3 = Header 2 [package=jst-2-pth]
  S2 = Toggle Switch [package=THT]
  S3 = Toggle Switch [package=THT]
  S4 = Toggle Switch [package=THT]
  J4 = female pin header, 2 pins [form="♀ (female)"]

nets:
  N1: LM2.Pin_0, J3.pin2, S2.COM, S3.COM, J4.pin2
  N2: LM2.Pin_1, J3.pin1, S2.L1, S3.L1, S4.L1, J4.pin1
  N3: LM2.Pin_2, JP3.2
  N4: LM2.Pin_3, JP3.1
  N5: S2.L2, S3.L2, S4.L2
